// Logisim project T8_project.circ as structural Verilog: 4 circuits, main circuit main
module main (
  input  in_1,
  input  in_2,
  input  in_3,
  input  in_4,
  input  ON_OFF_SWITCH
);

  wire clock_1_out, d_ff_1_q, d_ff_1_qn, hor_c_1_10_1_out_5, hor_c_1_10_1_out_6, hor_c_1_10_1_out_7,
       hor_c_1_10_1_out_8, hor_c_1_10_1_out_9, hor_c_1_10_1_out_10, hor_c_1_10_1_out_11, horc_light_1_out_5,
       horc_light_1_out_6, n31_sec_countdown_1_out_2, n31_sec_countdown_1_out_3, n31_sec_countdown_1_out_4,
       n31_sec_countdown_1_out_5, n31_sec_countdown_1_out_6, nor_1_out;

  Clock clock_1 (.out(clock_1_out));
  _31_sec_countdown u_31_sec_countdown_1 (
    .in_1(clock_1_out), .out_2(n31_sec_countdown_1_out_2), .out_3(n31_sec_countdown_1_out_3),
    .out_4(n31_sec_countdown_1_out_4), .out_5(n31_sec_countdown_1_out_5), .out_6(n31_sec_countdown_1_out_6));
  Hor_C_1_10 hor_c_1_10_1 (
    .A(in_1), .B(in_2), .C(in_3), .D(in_4), .out_5(hor_c_1_10_1_out_5), .out_6(hor_c_1_10_1_out_6),
    .out_7(hor_c_1_10_1_out_7), .out_8(hor_c_1_10_1_out_8), .out_9(hor_c_1_10_1_out_9),
    .out_10(hor_c_1_10_1_out_10), .out_11(hor_c_1_10_1_out_11));
  nor nor_1 (nor_1_out, n31_sec_countdown_1_out_2, n31_sec_countdown_1_out_3, n31_sec_countdown_1_out_4, n31_sec_countdown_1_out_5, n31_sec_countdown_1_out_6);
  _7_Segment_Display u_7_segment_display_1 (
    .g(hor_c_1_10_1_out_11), .f(hor_c_1_10_1_out_10), .a(hor_c_1_10_1_out_5), .b(hor_c_1_10_1_out_7),
    .e(hor_c_1_10_1_out_9), .d(hor_c_1_10_1_out_6), .c(hor_c_1_10_1_out_8));  // open: dp
  HorC_light horc_light_1 (
    .in_1(in_1), .out_5(horc_light_1_out_5), .in_2(in_2), .in_3(in_3), .in_4(in_4), .out_6(horc_light_1_out_6));
  D_Flip_Flop d_ff_1 (.clk(nor_1_out), .D(d_ff_1_qn), .Q(d_ff_1_q), .Qn(d_ff_1_qn));  // open: preset, en, reset
  not not_1 (horc_light_1_out_6, d_ff_1_q);
  LED led_1 (.in(horc_light_1_out_5));
  LED led_2 (.in(horc_light_1_out_6));
  not not_2 (horc_light_1_out_5, horc_light_1_out_6);

  // Notes on the sheet:
  //   INPUT
  //   TEMPERATURE OF ROOM
  //   C-COLD
  //   H-HOT
  //   -NORMAL
  //   TEMPERATURE CONTROL
  //   HEATER
  //   AIR CONDITIONER
  //   INSTRUCTIONS
  //   1.IF DISPLAY SHOWS H->AC WILL BE ON 
  //   2.IF DISPLAY SHOWS C->HEATER WILL BE ON
  //   3.IF DISPLAY SHOWS - BOTH WILL BE OFF
  //   4.IT WILL BE ON/OFF FOR 31 SEC
endmodule

module _31_sec_countdown (
  input  in_1,
  output out_2,
  output out_3,
  output out_4,
  output out_5,
  output out_6
);

  wire d_ff_1_qn, d_ff_2_qn, d_ff_3_qn, d_ff_4_qn, d_ff_5_qn;

  D_Flip_Flop d_ff_1 (.clk(in_1), .D(d_ff_1_qn), .Q(out_2), .Qn(d_ff_1_qn));  // open: preset, en, reset
  D_Flip_Flop d_ff_2 (.clk(out_2), .D(d_ff_2_qn), .Q(out_3), .Qn(d_ff_2_qn));  // open: preset, en, reset
  D_Flip_Flop d_ff_3 (.clk(out_3), .D(d_ff_3_qn), .Q(out_4), .Qn(d_ff_3_qn));  // open: preset, en, reset
  D_Flip_Flop d_ff_4 (.clk(out_4), .D(d_ff_4_qn), .Q(out_5), .Qn(d_ff_4_qn));  // open: preset, en, reset
  D_Flip_Flop d_ff_5 (.clk(out_5), .D(d_ff_5_qn), .Q(out_6), .Qn(d_ff_5_qn));  // open: preset, en, reset

  // Notes on the sheet:
  //   31 Sec Countdown
endmodule

module Hor_C_1_10 (
  input  A,
  input  B,
  input  C,
  input  D,
  output out_5,
  output out_6,
  output out_7,
  output out_8,
  output out_9,
  output out_10,
  output out_11
);

  wire A_prime_B_prime_out, A_prime_BC_out, A_prime_C_prime_out, AB_out, AB_prime_out, AC_out, AC_prime_out,
       AD_out, AD_prime_out, BC_prime_out, not_1_out, not_2_out, not_3_out, not_4_out;

  not not_1 (not_1_out, A);
  not not_2 (not_2_out, B);
  not not_3 (not_3_out, C);
  not not_4 (not_4_out, D);
  and A_prime_B_prime (A_prime_B_prime_out, not_1_out, not_2_out);
  and A_prime_C_prime (A_prime_C_prime_out, not_1_out, not_3_out);
  and AC_prime (AC_prime_out, A, not_3_out);
  and AC (AC_out, A, C);
  and BC_prime (BC_prime_out, B, not_3_out);
  and AB (AB_out, B, A);
  and AB_prime (AB_prime_out, A, not_2_out);
  and AD (AD_out, A, D);
  and AD_prime (AD_prime_out, A, not_4_out);
  and A_prime_BC (A_prime_BC_out, B, not_1_out, C);
  or or_1 (out_5, A_prime_B_prime_out, A_prime_C_prime_out);
  or or_2 (out_7, AC_prime_out, AC_out);
  or or_3 (out_9, A_prime_B_prime_out, BC_prime_out, AB_out, AB_prime_out);
  or or_4 (out_11, AD_out, AD_prime_out, A_prime_BC_out);

  assign out_6 = out_5;
  assign out_8 = out_7;
  assign out_10 = out_9;

  // Notes on the sheet:
  //   H or C 1-10
endmodule

module HorC_light (
  input  in_1,
  input  in_2,
  input  in_3,
  input  in_4,
  output out_5,
  output out_6
);

  wire A_prime_B_prime_out, A_prime_C_prime_out, AB_out, AB_prime_D_out, AB_prime_D_prime_out, not_1_out,
       not_2_out, not_3_out, not_4_out;

  not not_1 (not_1_out, in_1);
  not not_2 (not_2_out, in_2);
  not not_3 (not_3_out, in_3);
  not not_4 (not_4_out, in_4);
  and A_prime_B_prime (A_prime_B_prime_out, not_1_out, not_2_out);
  and A_prime_C_prime (A_prime_C_prime_out, not_1_out, not_3_out);
  and AB (AB_out, in_1, in_2);
  and AB_prime_D (AB_prime_D_out, in_1, not_2_out, in_4);
  and AB_prime_D_prime (AB_prime_D_prime_out, in_1, not_2_out, not_4_out);
  or heater (out_5, A_prime_B_prime_out, A_prime_C_prime_out);
  or AC (out_6, AB_out, AB_prime_D_out, AB_prime_D_prime_out);

  // Notes on the sheet:
  //   HorC-light
endmodule
