// Logisim project power-alarm.circ as structural Verilog: 1 circuit, main circuit main
module main (
  input  in_1,
  output [7:0] out_2
);

  wire clock_1_out, counter_1_carry;

  Clock clock_1 (.out(clock_1_out));
  Counter #(.max('h90)) counter_1 (
    .Q(out_2), .carry(counter_1_carry), .clk(clock_1_out), .clr(in_1));  // open: load, D, count
  LED led_1 (.in(counter_1_carry));

  // Notes on the sheet:
  //   INPUT POWER SOURCE
  //   RESET AFTER EVERY MONTH
  //   1-RESET
  //   0-INCREMENT
  //   POWER COUNTER WITH ALRAM
  //   ALRAM
endmodule
